// Logisim project cpu.circ as structural Verilog: 7 circuits, main circuit main
module main (
);

  wire and_2_out, and_5_out, and_6_out, and_7_out, buffer_1_out, buffer_2_out, button_1_out, clock_1_out,
       d_ff_5_q, d_ff_9_q, decoder_1_out3, decoder_1_out4, not_1_out, not_2_out, not_3_out, not_4_out,
       or_1_out, or_2_out, or_3_out, or_5_out, undriven;
  wire [2:0] and_1_out, and_4_out, counter_1_q, d_ff_2_q, d_ff_6_q, d_ff_10_q;
  wire [2:2] d_ff_1_q;
  wire [7:0] and_1_out_2, and_3_out, and_8_out, counter_2_q, decoder_2_out0, decoder_3_out0,
       demultiplexer_1_out0, demultiplexer_1_out1, demultiplexer_1_out2, demultiplexer_1_out3,
       demultiplexer_1_out4, demultiplexer_1_out5, demultiplexer_1_out6, demultiplexer_1_out7,
       multiplexer_2_out, or_4_out, register_1_q, register_2_q, register_3_q, register_4_q, register_5_q,
       register_6_q, register_7_q, rom_1_data;
  wire [7:7] decoder_1_out0, decoder_1_out2, or_6_out;

  Clock clock_1 (.out(clock_1_out));
  Decoder #(.select(3)) decoder_1 (
    .out0(decoder_1_out0[7]), .out2(decoder_1_out2[7]), .out3(decoder_1_out3), .out4(decoder_1_out4),
    .sel(counter_1_q), .en(1'b1));  // open: out1, out5, out6, out7
  or or_1 (or_1_out, button_1_out, decoder_1_out4);
  Counter #(.width(3), .max('h7)) counter_1 (
    .count(clock_1_out), .Q(counter_1_q), .clk(clock_1_out), .clr(or_1_out));  // open: load, D, carry
  or or_2 (or_2_out, decoder_1_out4, decoder_1_out0[7]);
  assign {and_1_out_2[7], and_1_out, and_1_out_2[3:0]} = {8{decoder_1_out0[7]}} & rom_1_data;  // AND_Gate and_1, 8 bits wide
  or or_3 (or_3_out, decoder_1_out3, button_1_out);
  buf buffer_1 (buffer_1_out, and_1_out_2[1]);
  not not_1 (not_1_out, and_1_out_2[2]);
  not not_2 (not_2_out, and_1_out_2[0]);
  not not_3 (not_3_out, and_1_out_2[3]);
  and and_2 (and_2_out, not_3_out, not_1_out, buffer_1_out, not_2_out);
  ROM rom_1 (.addr(counter_2_q), .data(rom_1_data));  // open: sel
  D_Flip_Flop d_ff_1 (
    .clk(and_2_out), .D(and_2_out), .Q(d_ff_1_q[2]), .en(clock_1_out), .reset(or_3_out));  // open: Qn, preset
  T_Flip_Flop t_ff_1 ();  // open: clk, T, Q, Qn, preset, reset, en
  D_Flip_Flop d_ff_2 (
    .clk(d_ff_1_q[2]), .D(and_1_out[0]), .Q(d_ff_2_q[0]), .en(d_ff_1_q[2]), .reset(or_3_out));  // open: Qn, preset
  D_Flip_Flop d_ff_3 (
    .clk(d_ff_1_q[2]), .D(and_1_out[1]), .Q(d_ff_2_q[1]), .en(d_ff_1_q[2]), .reset(or_3_out));  // open: Qn, preset
  D_Flip_Flop d_ff_4 (
    .clk(d_ff_1_q[2]), .D(and_1_out[2]), .Q(d_ff_2_q[2]), .en(d_ff_1_q[2]), .reset(or_3_out));  // open: Qn, preset
  assign and_3_out = {8{decoder_1_out2[7]}} & rom_1_data;  // AND_Gate and_3, 8 bits wide
  Decoder #(.select(3)) decoder_2 (
    .out0(decoder_2_out0[0]), .out1(decoder_2_out0[1]), .out2(decoder_2_out0[2]), .out3(decoder_2_out0[3]),
    .out4(decoder_2_out0[4]), .out5(decoder_2_out0[5]), .out6(decoder_2_out0[6]), .out7(decoder_2_out0[7]),
    .sel(d_ff_2_q), .en(d_ff_1_q[2]));
  assign or_4_out = decoder_3_out0 | decoder_2_out0;  // OR_Gate or_4, 8 bits wide
  assign and_4_out = {3{d_ff_1_q[2]}} & d_ff_2_q;  // AND_Gate and_4, 3 bits wide
  // Probe on and_4_out
  and and_5 (and_5_out, clock_1_out, or_2_out);
  Demultiplexer #(.select(3), .width(8)) demultiplexer_1 (
    .out0(demultiplexer_1_out0), .out1(demultiplexer_1_out1), .out2(demultiplexer_1_out2),
    .out3(demultiplexer_1_out3), .out4(demultiplexer_1_out4), .out5(demultiplexer_1_out5),
    .out6(demultiplexer_1_out6), .out7(demultiplexer_1_out7), .in(and_8_out), .sel(and_4_out),
    .en(d_ff_1_q[2]));
  and and_6 (and_6_out, decoder_2_out0[7], and_7_out);
  and and_7 (and_7_out, decoder_1_out2[7], clock_1_out);
  // Probe on demultiplexer_1_out0
  // Probe on demultiplexer_1_out1
  // Probe on demultiplexer_1_out2
  // Probe on demultiplexer_1_out3
  // Probe on demultiplexer_1_out4
  // Probe on demultiplexer_1_out5
  // Probe on demultiplexer_1_out6
  // Probe on demultiplexer_1_out7
  not not_4 (not_4_out, and_6_out);
  buf buffer_2 (buffer_2_out, and_6_out);
  // Probe on and_8_out
  Register register_1 (
    .D(demultiplexer_1_out0), .en(decoder_2_out0[0]), .Q(register_1_q), .clk(and_7_out));  // open: clr
  Register register_2 (
    .D(demultiplexer_1_out1), .en(decoder_2_out0[1]), .Q(register_2_q), .clk(and_7_out));  // open: clr
  Register register_3 (
    .D(demultiplexer_1_out2), .en(decoder_2_out0[2]), .Q(register_3_q), .clk(and_7_out));  // open: clr
  Register register_4 (
    .D(demultiplexer_1_out3), .en(decoder_2_out0[3]), .Q(register_4_q), .clk(and_7_out));  // open: clr
  Register register_5 (
    .D(demultiplexer_1_out4), .en(decoder_2_out0[4]), .Q(register_5_q), .clk(and_7_out));  // open: clr
  Register register_6 (
    .D(demultiplexer_1_out5), .en(decoder_2_out0[5]), .Q(register_6_q), .clk(and_7_out));  // open: clr
  Register register_7 (
    .D(demultiplexer_1_out6), .en(decoder_2_out0[6]), .Q(register_7_q), .clk(and_7_out));  // open: clr
  Counter counter_2 (
    .load(and_6_out), .D(demultiplexer_1_out7), .count(not_4_out), .Q(counter_2_q), .clk(or_5_out),
    .clr(button_1_out));  // open: carry
  or or_5 (or_5_out, buffer_2_out, and_5_out);
  Button button_1 (.out(button_1_out));
  assign and_8_out = {8{or_6_out[7]}} & multiplexer_2_out;  // AND_Gate and_8, 8 bits wide
  // Probe on register_1_q
  // Probe on register_2_q
  // Probe on register_3_q
  // Probe on register_4_q
  // Probe on register_5_q
  // Probe on register_6_q
  // Probe on register_7_q
  // Probe on counter_2_q
  Multiplexer #(.select(3), .width(8)) multiplexer_1 (
    .in0(register_1_q), .in1(register_2_q), .in2(register_3_q), .in3(register_4_q), .in4(register_5_q),
    .in5(register_6_q), .in6(register_7_q), .in7(counter_2_q), .sel(d_ff_2_q));  // open: out, en
  Multiplexer #(.select(3), .width(8)) multiplexer_2 (
    .in0(register_1_q), .in1(register_2_q), .in2(register_3_q), .in3(register_4_q), .in4(register_5_q),
    .in5(register_6_q), .in6(register_7_q), .in7(counter_2_q), .out(multiplexer_2_out), .sel(d_ff_6_q),
    .en(or_6_out[7]));
  Multiplexer #(.select(3), .width(8)) multiplexer_3 (
    .in0(register_1_q), .in1(register_2_q), .in2(register_3_q), .in3(register_4_q), .in4(register_5_q),
    .in5(register_6_q), .in6(register_7_q), .in7(counter_2_q), .sel(d_ff_10_q));  // open: out, en
  // Probe on multiplexer_2_out
  // Probe on d_ff_2_q
  // Probe on d_ff_6_q
  // Probe on d_ff_10_q
  D_Flip_Flop d_ff_5 (
    .clk(decoder_1_out2[7]), .D(decoder_1_out2[7]), .Q(d_ff_5_q), .reset(or_3_out));  // open: Qn, preset, en
  D_Flip_Flop d_ff_6 (
    .clk(or_6_out[7]), .D(and_3_out[4]), .Q(d_ff_6_q[0]), .en(or_6_out[7]), .reset(or_3_out));  // open: Qn, preset
  D_Flip_Flop d_ff_7 (
    .clk(or_6_out[7]), .D(and_3_out[5]), .Q(d_ff_6_q[1]), .en(or_6_out[7]), .reset(or_3_out));  // open: Qn, preset
  D_Flip_Flop d_ff_8 (
    .clk(or_6_out[7]), .D(and_3_out[6]), .Q(d_ff_6_q[2]), .en(or_6_out[7]), .reset(or_3_out));  // open: Qn, preset
  or or_6 (or_6_out[7], d_ff_5_q, decoder_1_out2[7]);
  Decoder #(.select(3)) decoder_3 (
    .out0(decoder_3_out0[0]), .out1(decoder_3_out0[1]), .out2(decoder_3_out0[2]), .out3(decoder_3_out0[3]),
    .out4(decoder_3_out0[4]), .out5(decoder_3_out0[5]), .out6(decoder_3_out0[6]), .out7(decoder_3_out0[7]),
    .sel(d_ff_6_q), .en(or_6_out[7]));
  D_Flip_Flop d_ff_9 (.clk(undriven), .D(undriven), .Q(d_ff_9_q), .reset(or_3_out));  // open: Qn, preset, en
  D_Flip_Flop d_ff_10 (
    .clk(d_ff_9_q), .D(and_3_out[0]), .Q(d_ff_10_q[0]), .en(d_ff_9_q), .reset(or_3_out));  // open: Qn, preset
  D_Flip_Flop d_ff_11 (
    .clk(d_ff_9_q), .D(and_3_out[1]), .Q(d_ff_10_q[1]), .en(d_ff_9_q), .reset(or_3_out));  // open: Qn, preset
  D_Flip_Flop d_ff_12 (
    .clk(d_ff_9_q), .D(and_3_out[2]), .Q(d_ff_10_q[2]), .en(d_ff_9_q), .reset(or_3_out));  // open: Qn, preset
  Decoder #(.select(3)) decoder_4 (
    .sel(d_ff_10_q), .en(d_ff_9_q));  // open: out0, out1, out2, out3, out4, out5, out6, out7

  // Notes on the sheet:
  //   jmp
  //   contents of rom_1 (hex, n*v repeats v):
  //   42 10 42 20 42 30 42 40 42 50 42 60 72 0 72 0 72 0 72 0 72 0 72 0 72 0 72 0 72 0 72 0 72 0 72 0 72 0
  //   72 0 72 0 72 0 72 0 72 0 72 0 72 0 72 0 72 0 72 0 72 0 72 0 72 0 72 0 72 0 72 0 72 0 72 0 72 0 72 0
  //   72 0 72 0 72 0 72 0 72 0 72 0 72 0 72 0 72 0 72 0 72 0 72 0 72 0 72 0 72 0 72 0 72 0 72 0 72 0 72 0
  //   72 0 72 0 72 0 72 0 72 0 72 0 72 0 72 0 72 0 72 0 72 0 72 0 72 0 72 0 72 0 72 0 72 0 72 0 72 0 72 0
  //   72 0 72 0 72 0 72 0 72 0 72 0 72 0 72 0 72 0 72 0 72 0 72 0 72 0 72 0 72 0 72 0 72 0 72 0 72 0 72 0
  //   72 0 72 0 72 0 72 0 72 0 72 0 72 0 72 0 72 0 72 0 72 0 72 0 72 0 72 0 72 0 72 0 72 0 72 0 72 0 72 0
  //   72 0 72 0 72 0 72 0 72 0 72 0 72 0 72 0 72
  //   3bit latch OP0
  //   registers
  //   R0
  //   R6
  //   reset
  //   3bit latch OP1
  //   3bit latch OP2
endmodule

module registers (
  input  in_1,
  input  [2:0] OUT0_ADDR,
  input  [2:0] OUT1_ADDR,
  input  [2:0] OUT2_ADDR,
  input  [7:0] INPUT0,
  input  [2:0] IN0_ADDR,
  input  [7:0] INPUT1,
  input  [2:0] IN1_ADDR,
  input  [7:0] INPUT2,
  input  [2:0] IN2_ADDR,
  input  OUT0_ENABLE,
  input  OUT1_ENABLE,
  input  OUT2_ENABLE,
  input  in0_ENABLE,
  input  in1_ENABLE,
  input  in2_ENABLE,
  input  CLOCK,
  input  LATCH_RESET,
  output [7:0] OUT0,
  output [7:0] OUT1,
  output [7:0] OUT2
);

  wire d_ff_1_q, d_ff_2_q, d_ff_3_q, d_ff_13_q, d_ff_14_q, d_ff_15_q, main_lala_1_e, main_lala_1_q,
       main_lala_1_r, main_lala_1_t, main_lala_1_u, main_lala_1_w, main_lala_1_y, or_3_out, or_4_out,
       or_5_out, or_6_out, or_9_out, or_10_out, or_12_out, or_14_out, or_17_out, or_18_out, or_19_out,
       or_20_out, or_21_out, or_22_out;
  wire [1:0] demultiplexer_1_out0, demultiplexer_1_out1, demultiplexer_1_out2, demultiplexer_1_out3,
       demultiplexer_1_out4, demultiplexer_1_out5, demultiplexer_1_out6, demultiplexer_1_out7,
       demultiplexer_2_out0, demultiplexer_2_out1, demultiplexer_2_out2, demultiplexer_2_out3,
       demultiplexer_2_out4, demultiplexer_2_out5, demultiplexer_2_out6, demultiplexer_2_out7,
       demultiplexer_3_out0, demultiplexer_3_out1, demultiplexer_3_out2, demultiplexer_3_out3,
       demultiplexer_3_out4, demultiplexer_3_out5, demultiplexer_3_out6, demultiplexer_3_out7, or_1_out,
       or_2_out, or_7_out, or_8_out, or_11_out, or_13_out, or_15_out, or_16_out;
  wire [2:0] d_ff_4_q, d_ff_7_q, d_ff_10_q, d_ff_16_q, d_ff_19_q, d_ff_22_q;
  wire [3:0] counter_1_q;
  wire [7:0] counter_2_q, decoder_1_out0, decoder_2_out0, decoder_3_out0, decoder_4_out0, decoder_5_out0,
       decoder_6_out0, multiplexer_1_out, multiplexer_2_out, multiplexer_3_out, multiplexer_4_out,
       multiplexer_5_out, multiplexer_6_out, multiplexer_7_out, register_1_q, register_2_q, register_3_q,
       register_4_q, register_5_q, register_6_q, register_7_q;

  Counter #(.width(4), .max('hf)) counter_1 (.count(in_1), .Q(counter_1_q), .clk(in_1));  // open: load, D, carry, clr
  main_lala main_lala_1 (
    .a(counter_1_q[0]), .b(counter_1_q[1]), .c(counter_1_q[2]), .d(counter_1_q[3]), .q(main_lala_1_q),
    .w(main_lala_1_w), .e(main_lala_1_e), .r(main_lala_1_r), .t(main_lala_1_t), .y(main_lala_1_y),
    .u(main_lala_1_u));
  _7_Segment_Display u_7_segment_display_1 (
    .g(main_lala_1_w), .f(main_lala_1_q), .a(main_lala_1_e), .b(main_lala_1_r), .e(main_lala_1_t),
    .d(main_lala_1_y), .c(main_lala_1_u));  // open: dp
  Multiplexer #(.select(2), .width(8)) multiplexer_1 (
    .in0(INPUT0), .in1(INPUT1), .in2(INPUT2), .out(multiplexer_1_out), .sel(or_1_out), .en(or_19_out));  // open: in3
  Multiplexer #(.select(2), .width(8)) multiplexer_2 (
    .in0(INPUT0), .in1(INPUT1), .in2(INPUT2), .out(multiplexer_2_out), .sel(or_2_out), .en(or_17_out));  // open: in3
  Multiplexer #(.select(2), .width(8)) multiplexer_3 (
    .in0(INPUT0), .in1(INPUT1), .in2(INPUT2), .out(multiplexer_3_out), .sel(or_7_out), .en(or_18_out));  // open: in3
  Multiplexer #(.select(2), .width(8)) multiplexer_4 (
    .in0(INPUT0), .in1(INPUT1), .in2(INPUT2), .out(multiplexer_4_out), .sel(or_8_out), .en(or_14_out));  // open: in3
  Multiplexer #(.select(2), .width(8)) multiplexer_5 (
    .in0(INPUT0), .in1(INPUT1), .in2(INPUT2), .out(multiplexer_5_out), .sel(or_11_out), .en(or_12_out));  // open: in3
  Multiplexer #(.select(2), .width(8)) multiplexer_6 (
    .in0(INPUT0), .in1(INPUT1), .in2(INPUT2), .out(multiplexer_6_out), .sel(or_13_out), .en(or_10_out));  // open: in3
  Multiplexer #(.select(2), .width(8)) multiplexer_7 (
    .in0(INPUT0), .in1(INPUT1), .in2(INPUT2), .out(multiplexer_7_out), .sel(or_15_out), .en(or_9_out));  // open: in3
  Multiplexer #(.select(2), .width(8)) multiplexer_8 (
    .in0(INPUT0), .in1(INPUT1), .in2(INPUT2), .sel(or_16_out), .en(or_6_out));  // open: in3, out
  assign or_1_out = demultiplexer_1_out0 | demultiplexer_2_out0 | demultiplexer_3_out0;  // OR_Gate or_1, 2 bits wide
  D_Flip_Flop d_ff_1 (.clk(in0_ENABLE), .D(in0_ENABLE), .Q(d_ff_1_q), .reset(LATCH_RESET));  // open: Qn, preset, en
  D_Flip_Flop d_ff_2 (.clk(in1_ENABLE), .D(in1_ENABLE), .Q(d_ff_2_q), .reset(LATCH_RESET));  // open: Qn, preset, en
  D_Flip_Flop d_ff_3 (.clk(in2_ENABLE), .D(in2_ENABLE), .Q(d_ff_3_q), .reset(LATCH_RESET));  // open: Qn, preset, en
  assign or_2_out = demultiplexer_1_out1 | demultiplexer_2_out1 | demultiplexer_3_out1;  // OR_Gate or_2, 2 bits wide
  Demultiplexer #(.select(3), .width(2), .disabled(0)) demultiplexer_1 (
    .out0(demultiplexer_1_out0), .out1(demultiplexer_1_out1), .out2(demultiplexer_1_out2),
    .out3(demultiplexer_1_out3), .out4(demultiplexer_1_out4), .out5(demultiplexer_1_out5),
    .out6(demultiplexer_1_out6), .out7(demultiplexer_1_out7), .in(2'b00), .sel(IN0_ADDR), .en(in0_ENABLE));
  D_Flip_Flop d_ff_4 (
    .clk(CLOCK), .D(IN0_ADDR[0]), .Q(d_ff_4_q[0]), .en(or_3_out), .reset(LATCH_RESET));  // open: Qn, preset
  D_Flip_Flop d_ff_5 (
    .clk(CLOCK), .D(IN0_ADDR[1]), .Q(d_ff_4_q[1]), .en(or_3_out), .reset(LATCH_RESET));  // open: Qn, preset
  D_Flip_Flop d_ff_6 (
    .clk(CLOCK), .D(IN0_ADDR[2]), .Q(d_ff_4_q[2]), .en(or_3_out), .reset(LATCH_RESET));  // open: Qn, preset
  or or_3 (or_3_out, d_ff_1_q, in0_ENABLE);
  D_Flip_Flop d_ff_7 (
    .clk(CLOCK), .D(IN1_ADDR[0]), .Q(d_ff_7_q[0]), .en(or_4_out), .reset(LATCH_RESET));  // open: Qn, preset
  D_Flip_Flop d_ff_8 (
    .clk(CLOCK), .D(IN1_ADDR[1]), .Q(d_ff_7_q[1]), .en(or_4_out), .reset(LATCH_RESET));  // open: Qn, preset
  D_Flip_Flop d_ff_9 (
    .clk(CLOCK), .D(IN1_ADDR[2]), .Q(d_ff_7_q[2]), .en(or_4_out), .reset(LATCH_RESET));  // open: Qn, preset
  or or_4 (or_4_out, d_ff_2_q, in1_ENABLE);
  D_Flip_Flop d_ff_10 (
    .clk(CLOCK), .D(IN2_ADDR[0]), .Q(d_ff_10_q[0]), .en(or_5_out), .reset(LATCH_RESET));  // open: Qn, preset
  D_Flip_Flop d_ff_11 (
    .clk(CLOCK), .D(IN2_ADDR[1]), .Q(d_ff_10_q[1]), .en(or_5_out), .reset(LATCH_RESET));  // open: Qn, preset
  D_Flip_Flop d_ff_12 (
    .clk(CLOCK), .D(IN2_ADDR[2]), .Q(d_ff_10_q[2]), .en(or_5_out), .reset(LATCH_RESET));  // open: Qn, preset
  or or_5 (or_5_out, d_ff_3_q, in2_ENABLE);
  or or_6 (or_6_out, decoder_3_out0[7], decoder_2_out0[7], decoder_1_out0[7]);
  assign or_7_out = demultiplexer_1_out2 | demultiplexer_2_out2 | demultiplexer_3_out2;  // OR_Gate or_7, 2 bits wide
  assign or_8_out = demultiplexer_1_out3 | demultiplexer_2_out3 | demultiplexer_3_out3;  // OR_Gate or_8, 2 bits wide
  Demultiplexer #(.select(3), .width(2), .disabled(0)) demultiplexer_2 (
    .out0(demultiplexer_2_out0), .out1(demultiplexer_2_out1), .out2(demultiplexer_2_out2),
    .out3(demultiplexer_2_out3), .out4(demultiplexer_2_out4), .out5(demultiplexer_2_out5),
    .out6(demultiplexer_2_out6), .out7(demultiplexer_2_out7), .in(2'b01), .sel(IN1_ADDR), .en(in1_ENABLE));
  or or_9 (or_9_out, decoder_3_out0[6], decoder_2_out0[6], decoder_1_out0[6]);
  or or_10 (or_10_out, decoder_3_out0[5], decoder_2_out0[5], decoder_1_out0[5]);
  assign or_11_out = demultiplexer_1_out4 | demultiplexer_2_out4 | demultiplexer_3_out4;  // OR_Gate or_11, 2 bits wide
  Decoder #(.select(3), .disabled(0)) decoder_1 (
    .out0(decoder_1_out0[0]), .out1(decoder_1_out0[1]), .out2(decoder_1_out0[2]), .out3(decoder_1_out0[3]),
    .out4(decoder_1_out0[4]), .out5(decoder_1_out0[5]), .out6(decoder_1_out0[6]), .out7(decoder_1_out0[7]),
    .sel(d_ff_4_q), .en(or_3_out));
  Decoder #(.select(3), .disabled(0)) decoder_2 (
    .out0(decoder_2_out0[0]), .out1(decoder_2_out0[1]), .out2(decoder_2_out0[2]), .out3(decoder_2_out0[3]),
    .out4(decoder_2_out0[4]), .out5(decoder_2_out0[5]), .out6(decoder_2_out0[6]), .out7(decoder_2_out0[7]),
    .sel(d_ff_7_q), .en(or_4_out));
  Decoder #(.select(3), .disabled(0)) decoder_3 (
    .out0(decoder_3_out0[0]), .out1(decoder_3_out0[1]), .out2(decoder_3_out0[2]), .out3(decoder_3_out0[3]),
    .out4(decoder_3_out0[4]), .out5(decoder_3_out0[5]), .out6(decoder_3_out0[6]), .out7(decoder_3_out0[7]),
    .sel(d_ff_10_q), .en(or_5_out));
  or or_12 (or_12_out, decoder_3_out0[4], decoder_2_out0[4], decoder_1_out0[4]);
  assign or_13_out = demultiplexer_1_out5 | demultiplexer_2_out5 | demultiplexer_3_out5;  // OR_Gate or_13, 2 bits wide
  Demultiplexer #(.select(3), .width(2), .disabled(0)) demultiplexer_3 (
    .out0(demultiplexer_3_out0), .out1(demultiplexer_3_out1), .out2(demultiplexer_3_out2),
    .out3(demultiplexer_3_out3), .out4(demultiplexer_3_out4), .out5(demultiplexer_3_out5),
    .out6(demultiplexer_3_out6), .out7(demultiplexer_3_out7), .in(2'b10), .sel(IN2_ADDR), .en(in2_ENABLE));
  or or_14 (or_14_out, decoder_3_out0[3], decoder_2_out0[3], decoder_1_out0[3]);
  assign or_15_out = demultiplexer_1_out6 | demultiplexer_2_out6 | demultiplexer_3_out6;  // OR_Gate or_15, 2 bits wide
  assign or_16_out = demultiplexer_1_out7 | demultiplexer_2_out7 | demultiplexer_3_out7;  // OR_Gate or_16, 2 bits wide
  or or_17 (or_17_out, decoder_3_out0[1], decoder_2_out0[1], decoder_1_out0[1]);
  or or_18 (or_18_out, decoder_3_out0[2], decoder_2_out0[2], decoder_1_out0[2]);
  or or_19 (or_19_out, decoder_3_out0[0], decoder_2_out0[0], decoder_1_out0[0]);
  // Probe on multiplexer_1_out
  // Probe on multiplexer_2_out
  // Probe on multiplexer_3_out
  // Probe on multiplexer_4_out
  // Probe on multiplexer_5_out
  // Probe on multiplexer_6_out
  // Probe on multiplexer_7_out
  // Probe on register_1_q
  Register register_1 (.D(multiplexer_1_out), .en(or_19_out), .Q(register_1_q), .clk(CLOCK));  // open: clr
  // Probe on register_2_q
  Register register_2 (.D(multiplexer_2_out), .en(or_17_out), .Q(register_2_q), .clk(CLOCK));  // open: clr
  // Probe on register_3_q
  Register register_3 (.D(multiplexer_3_out), .en(or_18_out), .Q(register_3_q), .clk(CLOCK));  // open: clr
  Register register_4 (.D(multiplexer_4_out), .en(or_14_out), .Q(register_4_q), .clk(CLOCK));  // open: clr
  // Probe on register_4_q
  // Probe on register_5_q
  Register register_5 (.D(multiplexer_5_out), .en(or_12_out), .Q(register_5_q), .clk(CLOCK));  // open: clr
  // Probe on register_6_q
  Register register_6 (.D(multiplexer_6_out), .en(or_10_out), .Q(register_6_q), .clk(CLOCK));  // open: clr
  // Probe on register_7_q
  Register register_7 (.D(multiplexer_7_out), .en(or_9_out), .Q(register_7_q), .clk(CLOCK));  // open: clr
  Counter counter_2 (.Q(counter_2_q));  // open: load, D, count, carry, clk, clr
  // Probe on counter_2_q
  Multiplexer #(.select(3), .width(8)) multiplexer_9 (
    .in0(register_1_q), .in1(register_2_q), .in2(register_3_q), .in3(register_4_q), .in4(register_5_q),
    .in5(register_6_q), .in6(register_7_q), .in7(counter_2_q), .out(OUT0), .sel(d_ff_16_q), .en(OUT0_ENABLE));
  // Probe on d_ff_16_q
  Multiplexer #(.select(3), .width(8)) multiplexer_10 (
    .in0(register_1_q), .in1(register_2_q), .in2(register_3_q), .in3(register_4_q), .in4(register_5_q),
    .in5(register_6_q), .in6(register_7_q), .in7(counter_2_q), .out(OUT1), .sel(d_ff_19_q), .en(OUT1_ENABLE));
  // Probe on d_ff_19_q
  Multiplexer #(.select(3), .width(8)) multiplexer_11 (
    .in0(register_1_q), .in1(register_2_q), .in2(register_3_q), .in3(register_4_q), .in4(register_5_q),
    .in5(register_6_q), .in6(register_7_q), .in7(counter_2_q), .out(OUT2), .sel(d_ff_22_q), .en(OUT2_ENABLE));
  // Probe on d_ff_22_q
  D_Flip_Flop d_ff_13 (.clk(OUT0_ENABLE), .D(OUT0_ENABLE), .Q(d_ff_13_q), .reset(LATCH_RESET));  // open: Qn, preset, en
  or or_20 (or_20_out, d_ff_13_q, OUT0_ENABLE);
  D_Flip_Flop d_ff_14 (.clk(OUT1_ENABLE), .D(OUT1_ENABLE), .Q(d_ff_14_q), .reset(LATCH_RESET));  // open: Qn, preset, en
  or or_21 (or_21_out, d_ff_14_q, OUT1_ENABLE);
  D_Flip_Flop d_ff_15 (.clk(OUT2_ENABLE), .D(OUT2_ENABLE), .Q(d_ff_15_q), .reset(LATCH_RESET));  // open: Qn, preset, en
  or or_22 (or_22_out, d_ff_15_q, OUT2_ENABLE);
  D_Flip_Flop d_ff_16 (
    .clk(CLOCK), .D(OUT0_ADDR[0]), .Q(d_ff_16_q[0]), .en(or_20_out), .reset(LATCH_RESET));  // open: Qn, preset
  D_Flip_Flop d_ff_17 (
    .clk(CLOCK), .D(OUT0_ADDR[1]), .Q(d_ff_16_q[1]), .en(or_20_out), .reset(LATCH_RESET));  // open: Qn, preset
  D_Flip_Flop d_ff_18 (
    .clk(CLOCK), .D(OUT0_ADDR[2]), .Q(d_ff_16_q[2]), .en(or_20_out), .reset(LATCH_RESET));  // open: Qn, preset
  D_Flip_Flop d_ff_19 (
    .clk(CLOCK), .D(OUT1_ADDR[0]), .Q(d_ff_19_q[0]), .en(or_21_out), .reset(LATCH_RESET));  // open: Qn, preset
  D_Flip_Flop d_ff_20 (
    .clk(CLOCK), .D(OUT1_ADDR[1]), .Q(d_ff_19_q[1]), .en(or_21_out), .reset(LATCH_RESET));  // open: Qn, preset
  D_Flip_Flop d_ff_21 (
    .clk(CLOCK), .D(OUT1_ADDR[2]), .Q(d_ff_19_q[2]), .en(or_21_out), .reset(LATCH_RESET));  // open: Qn, preset
  D_Flip_Flop d_ff_22 (
    .clk(CLOCK), .D(OUT2_ADDR[0]), .Q(d_ff_22_q[0]), .en(or_22_out), .reset(LATCH_RESET));  // open: Qn, preset
  D_Flip_Flop d_ff_23 (
    .clk(CLOCK), .D(OUT2_ADDR[1]), .Q(d_ff_22_q[1]), .en(or_22_out), .reset(LATCH_RESET));  // open: Qn, preset
  D_Flip_Flop d_ff_24 (
    .clk(CLOCK), .D(OUT2_ADDR[2]), .Q(d_ff_22_q[2]), .en(or_22_out), .reset(LATCH_RESET));  // open: Qn, preset
  Decoder #(.select(3)) decoder_4 (
    .out0(decoder_4_out0[0]), .out1(decoder_4_out0[1]), .out2(decoder_4_out0[2]), .out3(decoder_4_out0[3]),
    .out4(decoder_4_out0[4]), .out5(decoder_4_out0[5]), .out6(decoder_4_out0[6]), .out7(decoder_4_out0[7]),
    .sel(d_ff_16_q), .en(or_20_out));
  Decoder #(.select(3)) decoder_5 (
    .out0(decoder_5_out0[0]), .out1(decoder_5_out0[1]), .out2(decoder_5_out0[2]), .out3(decoder_5_out0[3]),
    .out4(decoder_5_out0[4]), .out5(decoder_5_out0[5]), .out6(decoder_5_out0[6]), .out7(decoder_5_out0[7]),
    .sel(d_ff_19_q), .en(or_21_out));
  Decoder #(.select(3)) decoder_6 (
    .out0(decoder_6_out0[0]), .out1(decoder_6_out0[1]), .out2(decoder_6_out0[2]), .out3(decoder_6_out0[3]),
    .out4(decoder_6_out0[4]), .out5(decoder_6_out0[5]), .out6(decoder_6_out0[6]), .out7(decoder_6_out0[7]),
    .sel(d_ff_22_q), .en(or_22_out));

  // Notes on the sheet:
  //   3bit latch o0
  //   3bit latch o1
  //   3bit latch o2
  //   registers
  //   R0
  //   R6
  //   3bit latch i0
  //   3bit latch i1
  //   3bit latch i2
endmodule

module mainasdf (
  input  saasdf,
  input  gfsdaf
);

  main main_1 ();
  registers registers_1 ();  // open: OUT0, OUT0_ADDR, OUT1, OUT1_ADDR, OUT2, OUT2_ADDR, INPUT0, IN0_ADDR, INPUT1, IN1_ADDR, INPUT2, IN2_ADDR, OUT0_ENABLE, CLOCK, LATCH_RESET, OUT1_ENABLE, OUT2_ENABLE, in0_ENABLE, in1_ENABLE, in2_ENABLE, in_1
  registers registers_2 ();  // open: OUT0, OUT0_ADDR, OUT1, OUT1_ADDR, OUT2, OUT2_ADDR, INPUT0, IN0_ADDR, INPUT1, IN1_ADDR, INPUT2, IN2_ADDR, OUT0_ENABLE, CLOCK, LATCH_RESET, OUT1_ENABLE, OUT2_ENABLE, in0_ENABLE, in1_ENABLE, in2_ENABLE, in_1
endmodule

module main_lala (
  input  a,
  input  b,
  input  c,
  input  d,
  output q,
  output w,
  output e,
  output r,
  output t,
  output y,
  output u
);

  wire nand_1_out, nand_2_out, nand_3_out, nand_4_out, nand_5_out, nand_6_out, nand_7_out, nand_8_out,
       nand_9_out, nand_10_out, nand_11_out, nand_12_out, nand_13_out, nand_14_out, nand_15_out, nand_16_out,
       nand_17_out, nand_18_out, nand_19_out, nand_20_out, nand_21_out, nand_22_out, nand_23_out,
       nand_24_out, nand_25_out, nand_26_out, nand_27_out, nand_28_out, nand_29_out, nand_30_out,
       nand_31_out, nand_32_out, nand_33_out, nand_34_out, nand_35_out, nand_36_out, nand_37_out,
       nand_38_out, nand_39_out, nand_40_out, nand_41_out, nand_42_out, nand_43_out, nand_44_out,
       nand_45_out, nand_46_out, nand_47_out, nand_48_out, nand_49_out, nand_50_out, nand_51_out,
       nand_52_out, nand_53_out, nand_54_out, nand_55_out, nand_56_out, nand_57_out, nand_58_out,
       nand_59_out, nand_60_out, nand_61_out, nand_62_out, nand_63_out, nand_64_out, nand_65_out,
       nand_66_out, nand_67_out, nand_68_out, nand_69_out, nand_70_out, nand_71_out, nand_72_out,
       nand_73_out, nand_74_out, nand_75_out, nand_76_out, nand_77_out, nand_78_out, nand_79_out,
       nand_80_out, nand_81_out, nand_82_out, nand_83_out, nand_84_out, nand_85_out, nand_86_out,
       nand_87_out, nand_88_out, nand_90_out, nand_91_out, nand_92_out, nand_93_out, nand_94_out,
       nand_95_out, nand_96_out, nand_97_out, nand_98_out, nand_99_out, nand_100_out, nand_101_out,
       nand_102_out, nand_103_out, nand_104_out, nand_105_out, nand_106_out, nand_107_out, nand_108_out,
       nand_109_out, nand_110_out, nand_111_out, nand_112_out, nand_117_out, nand_118_out, nand_119_out,
       nand_120_out, nand_121_out, nand_122_out;

  nand nand_1 (nand_1_out, b, b);
  nand nand_2 (nand_2_out, c, c);
  nand nand_3 (nand_3_out, a, a);
  nand nand_4 (nand_4_out, b, b);
  nand nand_5 (nand_5_out, c, c);
  nand nand_6 (nand_6_out, b, b);
  nand nand_7 (nand_7_out, a, a);
  nand nand_8 (nand_8_out, c, c);
  nand nand_9 (nand_9_out, a, a);
  nand nand_10 (nand_10_out, a, a);
  nand nand_11 (nand_11_out, c, c);
  nand nand_12 (nand_12_out, c, c);
  nand nand_13 (nand_13_out, b, b);
  nand nand_14 (nand_14_out, d, d);
  nand nand_15 (nand_15_out, a, a);
  nand nand_16 (nand_16_out, a, a);
  nand nand_17 (nand_17_out, b, b);
  nand nand_18 (nand_18_out, c, c);
  nand nand_19 (nand_19_out, nand_1_out, nand_2_out);
  nand nand_20 (nand_20_out, nand_3_out, b);
  nand nand_21 (nand_21_out, nand_4_out, nand_5_out);
  nand nand_22 (nand_22_out, nand_6_out, d);
  nand nand_23 (nand_23_out, b, c);
  nand nand_24 (nand_24_out, nand_7_out, nand_8_out);
  nand nand_25 (nand_25_out, nand_9_out, c);
  nand nand_26 (nand_26_out, nand_10_out, nand_11_out);
  nand nand_27 (nand_27_out, d, d);
  nand nand_28 (nand_28_out, b, nand_12_out);
  nand nand_29 (nand_29_out, a, c);
  nand nand_30 (nand_30_out, nand_13_out, nand_14_out);
  nand nand_31 (nand_31_out, nand_15_out, c);
  nand nand_32 (nand_32_out, nand_16_out, b);
  nand nand_33 (nand_33_out, nand_17_out, nand_18_out);
  nand nand_34 (nand_34_out, nand_19_out, nand_19_out);
  nand nand_35 (nand_35_out, d, d);
  nand nand_36 (nand_36_out, a, a);
  nand nand_37 (nand_37_out, b, b);
  nand nand_38 (nand_38_out, b, b);
  nand nand_39 (nand_39_out, d, d);
  nand nand_40 (nand_40_out, nand_20_out, nand_20_out);
  nand nand_41 (nand_41_out, d, d);
  nand nand_42 (nand_42_out, nand_21_out, nand_22_out);
  nand nand_43 (nand_43_out, nand_23_out, nand_23_out);
  nand nand_44 (nand_44_out, d, d);
  nand nand_45 (nand_45_out, b, b);
  nand nand_46 (nand_46_out, nand_24_out, nand_24_out);
  nand nand_47 (nand_47_out, nand_25_out, nand_25_out);
  nand nand_48 (nand_48_out, d, d);
  nand nand_49 (nand_49_out, nand_26_out, nand_27_out);
  nand nand_50 (nand_50_out, nand_28_out, nand_29_out);
  nand nand_51 (nand_51_out, nand_30_out, nand_31_out);
  nand nand_52 (nand_52_out, nand_32_out, nand_32_out);
  nand nand_53 (nand_53_out, c, c);
  nand nand_54 (nand_54_out, d, d);
  nand nand_55 (nand_55_out, nand_33_out, nand_33_out);
  nand nand_56 (nand_56_out, d, d);
  nand nand_57 (nand_57_out, nand_34_out, nand_35_out);
  nand nand_58 (nand_58_out, c, d);
  nand nand_59 (nand_59_out, nand_36_out, b);
  nand nand_60 (nand_60_out, a, nand_37_out);
  nand nand_61 (nand_61_out, a, b);
  nand nand_62 (nand_62_out, nand_38_out, nand_39_out);
  nand nand_63 (nand_63_out, nand_40_out, d);
  nand nand_64 (nand_64_out, a, nand_41_out);
  nand nand_65 (nand_65_out, nand_42_out, nand_42_out);
  nand nand_66 (nand_66_out, nand_43_out, nand_44_out);
  nand nand_67 (nand_67_out, a, nand_45_out);
  nand nand_68 (nand_68_out, a, d);
  nand nand_69 (nand_69_out, nand_46_out, d);
  nand nand_70 (nand_70_out, nand_47_out, nand_48_out);
  nand nand_71 (nand_71_out, nand_49_out, nand_49_out);
  nand nand_72 (nand_72_out, nand_50_out, nand_50_out);
  nand nand_73 (nand_73_out, nand_51_out, nand_51_out);
  nand nand_74 (nand_74_out, nand_52_out, d);
  nand nand_75 (nand_75_out, a, nand_53_out);
  nand nand_76 (nand_76_out, a, nand_54_out);
  nand nand_77 (nand_77_out, nand_55_out, d);
  nand nand_78 (nand_78_out, c, nand_56_out);
  nand nand_79 (nand_79_out, nand_57_out, nand_58_out);
  nand nand_80 (nand_80_out, nand_59_out, nand_59_out);
  nand nand_81 (nand_81_out, nand_60_out, nand_60_out);
  nand nand_82 (nand_82_out, d, d);
  nand nand_83 (nand_83_out, nand_61_out, nand_61_out);
  nand nand_84 (nand_84_out, nand_62_out, c);
  nand nand_85 (nand_85_out, nand_63_out, nand_64_out);
  nand nand_86 (nand_86_out, nand_65_out, nand_66_out);
  nand nand_87 (nand_87_out, nand_67_out, nand_68_out);
  nand nand_88 (nand_88_out, nand_69_out, nand_70_out);
  nand nand_89 (t, nand_71_out, nand_72_out);
  nand nand_90 (nand_90_out, nand_73_out, nand_74_out);
  nand nand_91 (nand_91_out, nand_75_out, nand_76_out);
  nand nand_92 (nand_92_out, nand_77_out, nand_78_out);
  nand nand_93 (nand_93_out, d, d);
  nand nand_94 (nand_94_out, b, b);
  nand nand_95 (nand_95_out, nand_79_out, nand_79_out);
  nand nand_96 (nand_96_out, nand_80_out, c);
  nand nand_97 (nand_97_out, nand_81_out, nand_82_out);
  nand nand_98 (nand_98_out, nand_83_out, d);
  nand nand_99 (nand_99_out, nand_84_out, nand_84_out);
  nand nand_100 (nand_100_out, nand_85_out, nand_85_out);
  nand nand_101 (nand_101_out, nand_86_out, nand_86_out);
  nand nand_102 (nand_102_out, nand_87_out, nand_87_out);
  nand nand_103 (nand_103_out, nand_88_out, nand_88_out);
  nand nand_104 (nand_104_out, b, b);
  nand nand_105 (nand_105_out, nand_90_out, nand_90_out);
  nand nand_106 (nand_106_out, nand_91_out, nand_91_out);
  nand nand_107 (nand_107_out, nand_92_out, nand_92_out);
  nand nand_108 (nand_108_out, b, nand_93_out);
  nand nand_109 (nand_109_out, a, nand_94_out);
  nand nand_110 (nand_110_out, a, c);
  nand nand_111 (nand_111_out, nand_95_out, nand_96_out);
  nand nand_112 (nand_112_out, nand_97_out, nand_98_out);
  nand nand_113 (w, nand_99_out, nand_100_out);
  nand nand_114 (e, nand_101_out, nand_102_out);
  nand nand_115 (r, nand_103_out, nand_104_out);
  nand nand_116 (y, nand_105_out, nand_106_out);
  nand nand_117 (nand_117_out, nand_107_out, nand_108_out);
  nand nand_118 (nand_118_out, nand_109_out, nand_110_out);
  nand nand_119 (nand_119_out, nand_111_out, nand_111_out);
  nand nand_120 (nand_120_out, nand_112_out, nand_112_out);
  nand nand_121 (nand_121_out, nand_117_out, nand_117_out);
  nand nand_122 (nand_122_out, nand_118_out, nand_118_out);
  nand nand_123 (q, nand_119_out, nand_120_out);
  nand nand_124 (u, nand_121_out, nand_122_out);
endmodule

module main_troll (
  input  a,
  input  b,
  input  c,
  input  d,
  output q,
  output w,
  output e,
  output r,
  output t,
  output y,
  output u
);

  wire and_1_out, and_2_out, and_3_out, and_4_out, and_5_out, and_6_out, and_7_out, and_8_out, and_9_out,
       and_10_out, and_11_out, and_12_out, and_13_out, and_14_out, and_15_out, and_16_out, and_17_out,
       and_18_out, and_19_out, and_20_out, and_21_out, and_22_out, and_23_out, and_24_out, and_25_out,
       and_26_out, and_27_out, and_28_out, not_1_out, not_2_out, not_3_out, not_4_out, not_5_out, not_6_out,
       not_7_out, not_8_out, not_9_out, not_10_out, not_11_out, not_12_out, not_13_out, not_14_out,
       not_15_out, not_16_out, not_17_out, not_18_out, not_19_out, not_20_out, not_21_out, not_22_out,
       not_23_out, not_24_out, not_25_out, not_26_out, not_27_out, not_28_out, not_29_out, not_30_out,
       not_31_out, not_32_out, not_33_out, not_34_out;

  not not_1 (not_1_out, b);
  and and_1 (and_1_out, not_1_out, not_2_out, not_3_out);
  not not_2 (not_2_out, c);
  not not_3 (not_3_out, d);
  and and_2 (and_2_out, c, d);
  not not_4 (not_4_out, a);
  and and_3 (and_3_out, not_4_out, b, c);
  and and_4 (and_4_out, a, not_5_out, not_6_out);
  not not_5 (not_5_out, b);
  not not_6 (not_6_out, d);
  and and_5 (and_5_out, a, b, d);
  not not_7 (not_7_out, b);
  and and_6 (and_6_out, not_7_out, not_8_out);
  not not_8 (not_8_out, d);
  not not_9 (not_9_out, c);
  not not_10 (not_10_out, a);
  and and_7 (and_7_out, not_10_out, b, d);
  and and_8 (and_8_out, a, not_11_out);
  not not_11 (not_11_out, d);
  not not_12 (not_12_out, b);
  and and_9 (and_9_out, not_12_out, not_13_out);
  not not_13 (not_13_out, c);
  not not_14 (not_14_out, b);
  and and_10 (and_10_out, not_14_out, d);
  and and_11 (and_11_out, b, c, not_15_out);
  not not_15 (not_15_out, d);
  and and_12 (and_12_out, a, not_16_out);
  not not_16 (not_16_out, b);
  and and_13 (and_13_out, a, d);
  not not_17 (not_17_out, a);
  not not_18 (not_18_out, c);
  and and_14 (and_14_out, not_17_out, not_18_out, d);
  not not_19 (not_19_out, a);
  and and_15 (and_15_out, not_19_out, c, not_20_out);
  not not_20 (not_20_out, d);
  not not_21 (not_21_out, a);
  and and_16 (and_16_out, not_21_out, not_22_out);
  not not_22 (not_22_out, c);
  and and_17 (and_17_out, b, not_23_out);
  not not_23 (not_23_out, c);
  and and_18 (and_18_out, a, c);
  not not_24 (not_24_out, b);
  and and_19 (and_19_out, not_24_out, not_25_out);
  not not_25 (not_25_out, d);
  not not_26 (not_26_out, a);
  and and_20 (and_20_out, not_26_out, c);
  not not_27 (not_27_out, a);
  and and_21 (and_21_out, not_27_out, b, d);
  and and_22 (and_22_out, a, not_28_out);
  not not_28 (not_28_out, c);
  and and_23 (and_23_out, a, not_29_out);
  not not_29 (not_29_out, d);
  not not_30 (not_30_out, b);
  not not_31 (not_31_out, c);
  and and_24 (and_24_out, not_30_out, not_31_out, d);
  and and_25 (and_25_out, c, not_32_out);
  not not_32 (not_32_out, d);
  and and_26 (and_26_out, b, not_33_out);
  not not_33 (not_33_out, d);
  and and_27 (and_27_out, a, not_34_out);
  not not_34 (not_34_out, b);
  and and_28 (and_28_out, a, c);
  or or_1 (q, and_1_out, and_2_out, and_3_out, and_4_out, and_5_out);
  or or_2 (w, and_6_out, not_9_out, and_7_out, and_8_out);
  or or_3 (e, and_9_out, and_10_out, and_11_out, and_12_out, and_13_out);
  or or_4 (r, and_14_out, and_15_out, b);
  or or_5 (t, and_16_out, d, and_17_out, and_18_out);
  or or_6 (y, and_19_out, and_20_out, and_21_out, and_22_out, and_23_out);
  or or_7 (u, and_24_out, and_25_out, and_26_out, and_27_out, and_28_out);
endmodule

module alu (
  input  [7:0] in_1,
  input  [7:0] in_2,
  input  add_sub,
  input  EN,
  output [7:0] out_5
);

  wire [7:0] adder_1_out, subtractor_1_out;

  Adder adder_1 (.a(in_1), .b(in_2), .out(adder_1_out));  // open: cin, cout
  Subtractor subtractor_1 (.a(in_1), .b(in_2), .out(subtractor_1_out));  // open: bin, bout
  Multiplexer #(.width(8)) multiplexer_1 (
    .in0(adder_1_out), .in1(subtractor_1_out), .out(out_5), .sel(add_sub), .en(EN));
endmodule

module fuha (
);

  wire and_1_out, and_2_out, button_1_out, clock_1_out, mov_1_out, nop_out, not_1_out, not_2_out, not_3_out,
       not_4_out, not_5_out, not_6_out, not_7_out, not_8_out, not_9_out, not_10_out, not_11_out, not_12_out,
       not_13_out, not_14_out, not_15_out, not_16_out, not_17_out, undriven, undriven_2, undriven_3;
  wire [1:0] counter_2_q, multiplexer_1_out;
  wire [7:0] bit_extender_1_out, ram_1_data, register_1_q;
  wire [23:0] counter_1_q;

  Clock clock_1 (.out(clock_1_out));
  Multiplexer #(.select(2), .width(2)) multiplexer_1 (
    .in0(2'b00), .in1(2'b01), .in2(2'b11), .out(multiplexer_1_out));  // open: in3, sel, en
  buf and_1 (and_1_out, clock_1_out);  // AND_Gate AND_Gate
  Counter #(.width(24), .max('hffffff)) counter_1 (
    .count(1'b1), .Q(counter_1_q), .clk(and_1_out), .clr(button_1_out));  // open: load, D, carry
  Button button_1 (.out(button_1_out));
  Bit_Extender #(.in_width(24), .out_width(8)) bit_extender_1 (.in(counter_1_q), .out(bit_extender_1_out));
  Counter #(.width(2), .max('h3)) counter_2 (
    .count(1'b1), .Q(counter_2_q), .clk(clock_1_out), .clr(undriven));  // open: load, D, carry
  Register register_1 (.D(ram_1_data), .en(undriven_3), .Q(register_1_q), .clk(clock_1_out), .clr(button_1_out));
  RAM ram_1 (.addr(bit_extender_1_out), .data(ram_1_data));  // open: sel, clk, ld, clr
  and and_2 (and_2_out, undriven_2, mov_1_out);
  not not_1 (not_1_out, register_1_q[1]);
  not not_2 (not_2_out, register_1_q[2]);
  not not_3 (not_3_out, register_1_q[0]);
  not not_4 (not_4_out, register_1_q[3]);
  and nop (nop_out, not_4_out, not_2_out, not_1_out, not_3_out);
  not not_5 (not_5_out, register_1_q[2]);
  not not_6 (not_6_out, register_1_q[3]);
  and mov_1 (mov_1_out, not_6_out, not_5_out, register_1_q[1], not_7_out);
  Register register_2 (.D(ram_1_data), .en(and_2_out), .clk(clock_1_out), .clr(button_1_out));  // open: Q
  not not_7 (not_7_out, register_1_q[0]);
  not not_8 (not_8_out, register_1_q[0]);
  // AND_Gate mov_2 has open pins: in0=register_1_q[3], in1=register_1_q[2], in2=register_1_q[1], in3=not_8_out, out=open
  Register register_3 ();  // open: D, en, Q, clk, clr
  not not_9 (not_9_out, register_1_q[3]);
  not not_10 (not_10_out, register_1_q[2]);
  // AND_Gate ld has open pins: in0=not_9_out, in1=not_10_out, in2=register_1_q[1], in3=register_1_q[0], out=open
  Register register_4 ();  // open: D, en, Q, clk, clr
  not not_11 (not_11_out, register_1_q[3]);
  not not_12 (not_12_out, register_1_q[1]);
  // AND_Gate st has open pins: in0=not_11_out, in1=register_1_q[2], in2=not_12_out, in3=not_13_out, out=open
  not not_13 (not_13_out, register_1_q[0]);
  not not_14 (not_14_out, register_1_q[0]);
  not not_15 (not_15_out, register_1_q[0]);
  // AND_Gate add has open pins: in0=not_15_out, in1=register_1_q[0], in2=register_1_q[0], in3=not_14_out, out=open
  not not_16 (not_16_out, register_1_q[3]);
  not not_17 (not_17_out, register_1_q[1]);
  // AND_Gate sub has open pins: in0=not_16_out, in1=register_1_q[2], in2=not_17_out, in3=register_1_q[0], out=open

  // Notes on the sheet:
  //   input latches
  //   instruction decoder
endmodule
